# Fritzing sketch estacionamento1.0 (saved by Fritzing 0.9.3b)
breadboards: 1

parts:
  Componente1 = Arduino Uno (Rev3) - ICSP
  U2 = TCRT5000 [package=THT]
  U3 = TCRT5000 [package=THT]
  U4 = TCRT5000 [package=THT]
  U5 = TCRT5000 [package=THT]
  LED1 = LED - 5mm [color="Green (555nm)" package="5 mm [THT]"]
  LED2 = LED - 5mm [color="Red (633nm)" package="5 mm [THT]"]
  LED3 = LED - 5mm [color="Green (555nm)" package="5 mm [THT]"]
  LED4 = LED - 5mm [color="Red (633nm)" package="5 mm [THT]"]
  LED5 = LED - 5mm [color="Green (555nm)" package="5 mm [THT]"]
  R1 = Resistor [tolerance=±5% resistance=220 package=THT]
  R2 = Resistor [tolerance=±5% resistance=220 package=THT]
  R3 = Resistor [tolerance=±5% resistance=220 package=THT]
  R4 = Resistor [tolerance=±5% resistance=220 package=THT]
  R5 = Resistor [tolerance=±5% resistance=220 package=THT]
  R6 = Resistor [tolerance=±5% resistance=220 package=THT]
  J1 = Basic Servo
  J2 = Basic Servo
  U1 = TCRT5000 [package=THT]
  R14 = Resistor [tolerance=±5% resistance=220 package=THT]
  R15 = Resistor [tolerance=±5% resistance=10k package=THT]
  R16 = Resistor [tolerance=±5% resistance=220 package=THT]
  R17 = Resistor [tolerance=±5% resistance=220 package=THT]
  R18 = Resistor [tolerance=±5% resistance=220 package=THT]
  R19 = Resistor [tolerance=±5% resistance=220 package=THT]
  LED6 = LED - 5mm [color="Red (633nm)" package="5 mm [THT]"]
  R20 = Resistor [tolerance=±5% resistance=10k package=THT]
  R21 = Resistor [tolerance=±5% resistance=10k package=THT]
  R22 = Resistor [tolerance=±5% resistance=10k package=THT]
  R23 = Resistor [tolerance=±5% resistance=10k package=THT]

nets:
  N1: Componente1.A0, U1.Pin_2, R15.Pin_0
  N2: Componente1.A1, U2.Pin_2, R20.Pin_0
  N3: Componente1.A2, U3.Pin_2, R21.Pin_0
  N4: Componente1.A3, U4.Pin_2, R22.Pin_0
  N5: Componente1.A4/SDA, U5.Pin_2, R23.Pin_0
  VCC: Componente1.5V, J1.vcc, J2.vcc, R14.Pin_1, R15.Pin_1, R16.Pin_1, R17.Pin_1, R18.Pin_1, R19.Pin_1, R20.Pin_1, R21.Pin_1, R22.Pin_1, R23.Pin_1
  N6: Componente1.D8, J1.pulse
  N7: Componente1.D9_PWM, J2.pulse
  N8: Componente1.D2, R1.Pin_0
  N9: Componente1.D3_PWM, R2.Pin_0
  N10: Componente1.D4, R3.Pin_0
  N11: Componente1.D5_PWM, R4.Pin_0
  N12: Componente1.D6_PWM, R5.Pin_0
  N13: Componente1.D7, R6.Pin_0
  GND: Componente1.GND, U2.Pin_1, U2.Pin_4, U3.Pin_1, U3.Pin_4, U4.Pin_1, U4.Pin_4, U5.Pin_1, U5.Pin_4, LED1.cathode, LED2.cathode, LED3.cathode, LED4.cathode, LED5.cathode, J1.gnd, J2.gnd, U1.Pin_1, U1.Pin_4, LED6.cathode
  N14: U2.Pin_3, R16.Pin_0
  N15: U3.Pin_3, R17.Pin_0
  N16: U4.Pin_3, R18.Pin_0
  N17: U5.Pin_3, R19.Pin_0
  N18: LED1.anode, R1.Pin_1
  N19: LED2.anode, R2.Pin_1
  N20: LED3.anode, R3.Pin_1
  N21: LED4.anode, R4.Pin_1
  N22: LED5.anode, R5.Pin_1
  N23: R6.Pin_1, LED6.anode
  N24: U1.Pin_3, R14.Pin_0

custom parts:
  TCRT5000: TCRT5000 optical reflective sensor
